// Logisim project Fetch.circ as structural Verilog: 1 circuit, main circuit Fetch
module Fetch (
  input  clk,
  input  reset,
  output [31:0] inst_out
);

  wire [31:0] adder_1_out, PC_q;

  Register #(.width(32)) PC (.D(adder_1_out), .Q(PC_q), .clk(clk), .clr(reset));  // open: en
  Adder #(.width(32)) adder_1 (.a(32'h4), .b(PC_q), .out(adder_1_out));  // open: cin, cout
  RAM #(.addrWidth(24), .dataWidth(32), .bus("asynch")) ram_1 (
    .addr(PC_q[25:2]), .data(inst_out));  // open: sel, ld, clr
endmodule
